// Logisim project 8bitcomputer.circ as structural Verilog: 2 circuits, main circuit main
module AU (
  input  [7:0] N1,
  input  C_IN,
  input  SUB,
  input  [7:0] N2,
  output [7:0] SUM,
  output C_OUT,
  output ZERO,
  output NEG
);

  wire not_1_out;
  wire [7:0] controlled_buffer_1_out, controlled_buffer_2_out;

  not not_1 (not_1_out, SUB);
  assign controlled_buffer_1_out = SUB ? N2 : 8'bz;  // Controlled_Buffer controlled_buffer_1
  assign controlled_buffer_2_out = not_1_out ? N2 : 8'bz;  // Controlled_Buffer controlled_buffer_2
  Negator negator_1 (.in(controlled_buffer_1_out), .out(controlled_buffer_2_out));
  Adder adder_1 (.a(N1), .b(controlled_buffer_2_out), .out({NEG, SUM[6:0]}), .cin(C_IN), .cout(C_OUT));
  or or_1 (ZERO, SUM[0], SUM[1], SUM[2], SUM[3], SUM[4], SUM[5], SUM[6], NEG);

  assign SUM[7] = NEG;
endmodule

module main (
);

  wire AOUT, button_1_out, button_2_out, button_3_out, button_4_out, button_5_out, button_6_out, CI, CLK,
       clock_1_out, COL, HLT, LFM, MO, not_1_out, or_2_out, ORI, R1_IN, R1_OUT, RADL, STM, SUB, XI, XO, YI,
       YO;
  wire [2:0] MI_Counter_q;
  wire [7:0] au_1_sum, controlled_buffer_1_out, counter_1_q, Data_RAM_dout, OUT_Register_q, Program_ROM_data,
       Program_ROM_data_2, R1_Register_q, register_1_q, X_Register_q, Y_Register_q;

  Clock clock_1 (.out(clock_1_out));
  or or_1 (CLK, clock_1_out, HLT);
  Register X_Register (.D(controlled_buffer_1_out), .en(XI), .clk(CLK), .Q(X_Register_q), .clr(button_1_out));
  Register Y_Register (.D(controlled_buffer_1_out), .en(YI), .clk(CLK), .Q(Y_Register_q), .clr(button_2_out));
  Button button_1 (.out(button_1_out));
  Button button_2 (.out(button_2_out));
  Register R1_Register (.D(controlled_buffer_1_out), .en(R1_IN), .clk(CLK), .Q(R1_Register_q), .clr(button_3_out));
  Button button_3 (.out(button_3_out));
  assign controlled_buffer_1_out = XO ? X_Register_q : 8'bz;  // Controlled_Buffer controlled_buffer_1
  AU au_1 (.SUM(au_1_sum), .N2(Y_Register_q), .N1(X_Register_q), .SUB(SUB));  // open: C_OUT, NEG, ZERO, C_IN
  assign controlled_buffer_1_out = YO ? Y_Register_q : 8'bz;  // Controlled_Buffer controlled_buffer_2
  assign controlled_buffer_1_out = R1_OUT ? R1_Register_q : 8'bz;  // Controlled_Buffer controlled_buffer_3
  assign controlled_buffer_1_out = AOUT ? au_1_sum : 8'bz;  // Controlled_Buffer controlled_buffer_4
  assign controlled_buffer_1_out = MO ? Program_ROM_data : 8'bz;  // Controlled_Buffer controlled_buffer_5
  Register OUT_Register (.D(controlled_buffer_1_out), .en(ORI), .clk(CLK), .Q(OUT_Register_q), .clr(button_5_out));
  Counter #(.max('h7), .width(3)) MI_Counter (
    .Q(MI_Counter_q), .clk(CLK), .clr(CI));  // open: load, D, count, carry, up
  Button button_4 (.out(button_4_out));
  Counter counter_1 (
    .clr(button_4_out), .load(COL), .up(1'b1), .clk(or_2_out), .D(controlled_buffer_1_out), .Q(counter_1_q));  // open: count, carry
  or or_2 (or_2_out, COL, CI);
  Button button_5 (.out(button_5_out));
  PLA #(.in_width(11), .out_width(16), .\table ("00000000000 0000000000000000 # NOP\n00000000001 0000000000000010\n00000001000 0000100000000100 # LDX\n00000001001 0000000000000010\n00000010000 0000010000001000 # XOUT\n00000010001 0000000000000010\n00000011000 0000001000000100 # LDY\n00000011001 0000000000000010\n00000100000 0000000100001000 # YOUT\n00000100001 0000000000000010\n00000101000 0000000010000100 # LDR\n00000101001 0000000000000010\n00000110000 0000000001001000 # ROUT\n00000110001 0000000000000010\n00000111000 0000010010000000 # SWP\n00000111001 0000100100000000\n00000111010 0000001001000000\n00000111011 0000000000000010\n00001000000 0000000000101000 # AOUT\n00001000001 0000000000000010\n00001001000 0000000000111000 # SOUT\n00001001001 0000000000000010\n00001010000 0000000000000101 # JMP\n00001011000 0000000010100000 # ATX\n00001011001 0000100001000000\n00001011010 0000000000000010\n00001100000 0000000010100000 # ATY\n00001100001 0000001001000000\n00001100010 0000000000000010\n00001101000 0000000010110000 # STX\n00001101001 0000100001000000\n00001101010 0000000000000010\n00001110000 0000000010110000 # STY\n00001110001 0000001001000000\n00001110010 0000000000000010\n00001111000 0000010010000000 # XTR\n00001111001 0000000000000010\n00010000000 0000000110000000 # YTR\n00010000001 0000000000000010\n00010001000 0000100001000000 # RTX\n00010001001 0000000000000010\n00010010000 0000001001000000 # RTY\n00010010001 0000000000000010\n00010011000 0000000010100000 # ATR\n00010011001 0000000000000010\n00010100000 0000000010110000 # STR\n00010100001 0000000000000010\n00010101000 0010000000000100 # SAD\n00010101001 0000000000000010\n00010110000 0000000000000000 # XLM\n00010110001 0100100000000000\n00010110010 0000000000000010\n00010111000 1000010000000000 # XTM\n00010111001 0000000000000010\n00011000000 0000000000000000 # RLM\n00011000001 0100000010000000\n00011000010 0000000000000010\n00011001000 1000000001000000 # RTM\n00011001001 0000000000000010\n00011010000 0000000000000000 # YLM\n00011010001 0100001000000000\n00011010010 0000000000000010\n00011011000 1000000100000000 # YTM\n00011011001 0000000000000010\n00011100000 0010000001000000 # SADR\n00011100001 0000000000000010\n00011101000 0010010000000000 # SADX\n00011101001 0000000000000010\n00011110000 0010000100000000 # SADY\n00011110001 0000000000000010\n10000000000 0001000000000000 # HLT")) MicroInstruction_PROM (
    .in({Program_ROM_data_2, MI_Counter_q}),
    .out({STM, LFM, RADL, HLT, XI, XO, YI, YO, R1_IN, R1_OUT, AOUT, SUB, ORI, MO, CI, COL}));
  Register register_1 (.D(controlled_buffer_1_out), .en(RADL), .clk(CLK), .Q(register_1_q), .clr(button_6_out));
  Button button_6 (.out(button_6_out));
  Hex_Digit_Display hex_digit_display_1 (.value(OUT_Register_q[7:4]));  // open: dp
  Hex_Digit_Display hex_digit_display_2 (.value(OUT_Register_q[3:0]));  // open: dp
  ROM #(.dataWidth(16)) Program_ROM (.addr(counter_1_q), .data({Program_ROM_data_2, Program_ROM_data}));
  assign controlled_buffer_1_out = LFM ? Data_RAM_dout : 8'bz;  // Controlled_Buffer controlled_buffer_6
  not not_1 (not_1_out, STM);
  RAM Data_RAM (
    .addr(register_1_q), .we(STM), .oe(not_1_out), .clk(CLK), .din(controlled_buffer_1_out),
    .dout(Data_RAM_dout));

  // Notes on the sheet:
  //   Registers and AU
  //   OpCode
  //   BUS
  //   Data
  //   on carry
  //   clear automatically
  //   Instruction Control
  //   contents of Program_ROM (hex, n*v repeats v):
  //   100 301 50f 1d00 1900 1300 1100 a02
  //   Program_ROM
endmodule
